# Fritzing sketch Pool-Sensor v2 (saved by Fritzing 1.0.3b)
breadboards: 1

parts:
  DS1 = DS18B20 1-Wire Temperature Sensor [part_number=DS18B20]
  Part1 = Arduino Uno (Rev3)
  R1 = Resistor [tolerance=±5% power=0.25W resistance=4.7 package=THT]
  LED1 = LEDs [package=led10mm]  # not connected

nets:
  GND: DS1.GND, Part1.GND
  N1: DS1.DQ, Part1.D2, R1.Pin_1
  VDD: DS1.VDD, Part1.5V, R1.Pin_0
